# Fritzing sketch diagram (saved by Fritzing 0.9.2b)
circuit board: 3.54185cm x 4.98119cm
breadboards: 1

parts:
  Q1 = Basic FET N-Channel [package="TO220 [THT]"]
  U1 = Voltage Regulator [package=to220-adj]
  Power_plug1 = Power plug
  Power_plug2 = Power plug
  Composant3 = Arduino Nano (Rev3.0)
  S1 = Pushbutton [package="[THT]"]
  R1 = Resistor [tolerance=±0.05% resistance=100k package="2010 [SMD]"]
  U2 = XD-RF-5V [package=THT]

nets (from the breadboard view):
  N1: Q1.gate, Composant3.D3, R1.Pin_0
  N2: Q1.drain, Power_plug2.GND
  GND: Q1.source, U1.IN, Power_plug1.GND, Composant3.GND, S1.Pin_1, S1.Pin_2, R1.Pin_1, U2.GND
  VCC: U1.ADJ, Power_plug1.VCC, Power_plug2.VCC
  VIN: U1.OUT, Composant3.VIN, U2.VCC
  N3: Composant3.D2, U2.DATA
  N4: Composant3.D4, S1.Pin_3, S1.Pin_4

notes:
  OUTPUT - 12V PWM
  INPUT - 12V

custom parts:
  XD-RF-5V: This is 433Mhz RF transmitter with receiver kit for Arduino ARM MCU wireless Application environment: Remote control switch, receiver module, motorcycles, automobile anti-theft products, home security products, electric doors, shutter doors, windows, remote control socket, remote control LED, remote audio remote control electric doors, garage door remote control, remote control retractable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
